// Logisim project alu.circ as structural Verilog: 1 circuit, main circuit alu
module alu (
  input  [31:0] A,
  input  [31:0] B,
  input  [3:0] ALUSel,
  output [31:0] Result
);

  wire adder_1_cout, comparator_1_lt;
  wire [4:0] B_SELECT, bitfinder_1_index;
  wire [5:0] undriven;
  wire [31:0] add0, and0, bsel, divu, mul, mulh, mulhu, multiplier_1_cout, multiplier_3_cout,
       multiplier_3_out, or0, remu, shifter_4_out, sll0, slt0, sra0, srl0, sub, xor0;

  // Probe on B
  // Probe on A
  BitSelector #(.width(32), .group(5)) bitselector_1 (.in(B), .out(B_SELECT), .sel(3'b000));
  Adder #(.width(32)) adder_1 (.a(A), .b(B), .out(add0), .cout(adder_1_cout));  // open: cin
  assign and0 = A & B;  // AND_Gate and_1, 32 bits wide
  Shifter #(.width(32)) shifter_1 (.in(A), .\dist (B_SELECT), .out(sll0));
  Comparator #(.width(32)) comparator_1 (.a(A), .b(B), .lt(comparator_1_lt));  // open: gt, eq
  Divider #(.width(32)) divider_1 (.a(A), .b(B), .rem(remu));  // open: out, upper
  Multiplier #(.width(32)) multiplier_1 (.a(A), .b(B), .out(mul), .cout(multiplier_1_cout));  // open: cin
  assign or0 = A | B;  // OR_Gate or_1, 32 bits wide
  assign xor0 = A ^ B;  // XOR_Gate xor_1, 32 bits wide
  Shifter #(.width(32), .shift("lr")) shifter_2 (.in(A), .\dist (B_SELECT), .out(srl0));
  Shifter #(.width(32), .shift("ar")) shifter_3 (.in(A), .\dist (B_SELECT), .out(sra0));
  Divider #(.width(32)) divider_2 (.a(A), .b(B), .out(divu));  // open: upper, rem
  // Probe on multiplier_1_cout
  // Probe on comparator_1_lt
  Multiplexer #(.width(32)) multiplexer_1 (
    .in0({32{1'b0}}), .in1(32'h1), .out(slt0), .sel(comparator_1_lt));  // open: en
  Multiplier #(.width(32)) multiplier_2 (.a(A), .b(B), .cout(mulhu));  // open: out, cin
  Subtractor #(.width(32)) subtractor_1 (.a(A), .b(B), .out(sub));  // open: bin, bout
  Multiplexer #(.width(32), .enable("false")) multiplexer_2 (.in0(A), .in1(B), .out(bsel), .sel(1'b1));
  Multiplexer #(.select(4), .width(32)) multiplexer_3 (
    .in0(add0), .in1(and0), .in2(or0), .in3(xor0), .in4(srl0), .in5(sra0), .in6(sll0), .in7(slt0),
    .in8(divu), .in9(remu), .in10(mul), .in11(mulhu), .in12(sub), .in13(bsel), .in14(mulh), .out(Result),
    .sel(ALUSel));  // open: in15, en
  Multiplier #(.width(32)) multiplier_3 (.a(A), .b(B), .out(multiplier_3_out), .cout(multiplier_3_cout));  // open: cin
  // Probe on multiplier_3_out
  Shifter #(.width(32), .shift("ar")) shifter_4 (.in(multiplier_3_cout), .out(shifter_4_out));  // open: dist
  BitFinder #(.width(32), .\type ("high1")) bitfinder_1 (
    .in(multiplier_3_cout), .index(bitfinder_1_index));  // open: found
  // Probe on Result
  // Probe on shifter_4_out
  // Probe on bitfinder_1_index
  assign shifter_4_out = {{26{undriven[5]}}, undriven};  // Bit_Extender bit_extender_1
  // Probe on nothing

  // Other names for the same wires on the sheet: SHIFT_B[31:0] = B; UNSIGN_A[31:0] = A

  // Notes on the sheet:
  //   INPUTS to your circuit (2's comp)
  //   0 = ADD
  //   1 = AND 
  //   2 = OR 
  //   3 = XOR
  //   4 = SRL
  //   5 = SRA
  //   6 = SLL
  //   7 = SLT
  //   8  = DIVU
  //   9 - REMU
  //   10 = MUL
  //   11 = MULHU
  //   12 = SUB
  //   13 = BSEL 
  //   14 =  MULH
  //   Select the first 5 bits of B.
  //   DON'T CHANGE THE LOCATIONS OF THE INPUTS AND OUTPUTS!
  //   11-13: MULHU -> BSEL
  //   OUTPUT from your circuit
endmodule
