// Logisim project cpu.circ as structural Verilog: 5 circuits, main circuit main
module main (
  input  [31:0] INSTRUCTION,
  input  CLOCK,
  output [31:0] PROGRAM_COUNTER,
  output [31:0] ra,
  output [31:0] sp,
  output [31:0] t0,
  output [31:0] t1,
  output [31:0] t2,
  output [31:0] s0,
  output [31:0] s1,
  output [31:0] a0
);

  wire ASEL, BrEq, BrLT, BrUn, BSEL, MEMRW, PCSEL, RegWEn, undriven, undriven_2;
  wire [1:0] WBSEL;
  wire [2:0] IMMSEL;
  wire [3:0] ALUSEL;
  wire [31:0] adder_1_out, ALU_OUT, imm, multiplexer_1_out, multiplexer_2_out, multiplexer_3_out,
       multiplexer_4_out, multiplexer_5_out, PC, PC_PLUS_4_TELEPORT, ReadData, RegFile_read_data_1,
       register_3_q, wd;

  // Probe on undriven
  Adder #(.width(32)) adder_1 (.a(PROGRAM_COUNTER), .b(32'h4), .out(adder_1_out));  // open: cin, cout
  Multiplexer #(.width(32), .enable("false")) multiplexer_1 (
    .in0(adder_1_out), .in1(ALU_OUT), .out(multiplexer_1_out), .sel(PCSEL));
  Register #(.width(32)) register_1 (
    .D(multiplexer_1_out), .en(undriven_2), .clk(CLOCK), .Q(PROGRAM_COUNTER));  // open: clr
  Register #(.width(32)) register_2 (.D(PROGRAM_COUNTER), .clk(CLOCK), .Q(PC));  // open: en, clr
  Multiplexer #(.width(32), .enable("false")) multiplexer_2 (
    .in0(INSTRUCTION), .in1(32'h13), .out(multiplexer_2_out), .sel(PCSEL));
  Adder #(.width(32)) adder_2 (.a(32'h4), .b(PC), .out(PC_PLUS_4_TELEPORT));  // open: cin, cout
  Register #(.width(32)) register_3 (.D(multiplexer_2_out), .clk(CLOCK), .Q(register_3_q));  // open: en, clr
  // Probe on register_3_q[11:7]
  // Probe on register_3_q[19:15]
  // Probe on IMMSEL
  Control control_1 (
    .INSTRUCTION(register_3_q), .BrEq(BrEq), .BrLT(BrLT), .PCSEL(PCSEL), .IMMSEL(IMMSEL), .REGWEN(RegWEn),
    .BSEL(BSEL), .ASEL(ASEL), .ALUSEL(ALUSEL), .MEMRW(MEMRW), .WBSEL(WBSEL), .BrUn(BrUn));
  // Probe on INSTRUCTION
  ImmGen IMMEDIATE_GENERATOR (.INSTRUCTION(register_3_q), .IMMSEL(IMMSEL), .IMMEDIATE_GENERATED(imm));  // open: in_2
  // Probe on imm
  // Probe on RegFile_read_data_1
  regfile_main RegFile (
    .rs2(register_3_q[24:20]), .rd(register_3_q[11:7]), .Read_Data_1(RegFile_read_data_1), .Read_Data_2(wd),
    .ra(ra), .sp(sp), .t0(t0), .t1(t1), .t2(t2), .s0(s0), .s1(s1), .a0(a0), .rs1(register_3_q[19:15]),
    .Write_Data(multiplexer_5_out), .RegWEn(RegWEn), .clk(CLOCK));
  Multiplexer #(.width(32), .enable("false")) multiplexer_3 (
    .in0(RegFile_read_data_1), .in1(PC), .out(multiplexer_3_out), .sel(ASEL));
  Multiplexer #(.width(32), .enable("false")) multiplexer_4 (.in0(wd), .in1(imm), .out(multiplexer_4_out), .sel(BSEL));
  BranchComp branchcomp_1 (.DataA(RegFile_read_data_1), .DataB(wd), .BrUn(BrUn), .BrLT(BrLT), .BrEq(BrEq));
  alu Arithmetic_Logic_Unit (.B(multiplexer_4_out), .Result(ALU_OUT), .A(multiplexer_3_out), .ALUSel(ALUSEL));
  // Probe on ALU_OUT
  Multiplexer #(.select(2), .width(32), .enable("false")) multiplexer_5 (
    .in0(ReadData), .in1(ALU_OUT), .in2(PC_PLUS_4_TELEPORT), .out(multiplexer_5_out), .sel(WBSEL));  // open: in3
  // mem_main DMEM: pin names not known; wires that end beside it: ALU_OUT, wd, CLOCK, MEMRW, ReadData

  // Other names for the same wires on the sheet: clk = CLOCK

  // Notes on the sheet:
  //   Decide whether or not to kill instruction
  //   Output
  //   IMEM (do **NOT** move this)
  //   Inputs
  //   Inputs/Outputs for testing. Do **NOT** move these.
endmodule

module Control (
  input  [31:0] INSTRUCTION,
  input  BrEq,
  input  BrLT,
  output PCSEL,
  output [2:0] IMMSEL,
  output REGWEN,
  output BSEL,
  output ASEL,
  output [3:0] ALUSEL,
  output MEMRW,
  output [1:0] WBSEL,
  output BrUn
);

  wire add, addi, and0, and_31_out, andi, beq, blt, bltu, bne, comparator_1_eq, comparator_2_eq,
       comparator_3_eq, comparator_4_eq, comparator_5_eq, comparator_6_eq, comparator_9_eq, comparator_10_eq,
       comparator_11_eq, comparator_12_eq, comparator_13_eq, comparator_14_eq, comparator_15_eq,
       comparator_16_eq, comparator_17_eq, comparator_18_eq, comparator_19_eq, comparator_20_eq,
       comparator_21_eq, comparator_22_eq, comparator_23_eq, comparator_24_eq, comparator_25_eq,
       comparator_26_eq, comparator_27_eq, comparator_28_eq, comparator_29_eq, comparator_30_eq,
       comparator_31_eq, comparator_32_eq, comparator_33_eq, comparator_34_eq, comparator_35_eq,
       comparator_36_eq, comparator_37_eq, comparator_38_eq, comparator_39_eq, comparator_40_eq,
       comparator_41_eq, comparator_42_eq, comparator_43_eq, comparator_44_eq, comparator_45_eq,
       comparator_46_eq, comparator_47_eq, comparator_48_eq, comparator_49_eq, comparator_50_eq,
       comparator_51_eq, comparator_52_eq, comparator_53_eq, comparator_54_eq, comparator_55_eq,
       comparator_56_gt, comparator_56_lt, divu, I_TYPE, I_TYPE_LOAD, jal, jalr, JALR_I_TYPE, lb, lh, lui,
       lw, mul, mulh, mulhu, multiplexer_1_out, multiplexer_9_out, not_2_out, or0, or_2_out, or_4_out,
       or_5_out, or_6_out, ori, R_TYPE, remu, SB_TYPE, sll0, slli, slt, slti, srai, srl0, srli, sub, sw,
       U_TYPE, UJ_TYPE, xor0, xori;
  wire [1:0] multiplexer_11_out, multiplexer_15_out;
  wire [2:0] multiplexer_6_out, multiplexer_10_out, multiplexer_14_out, multiplexer_17_out,
       multiplexer_19_out;
  wire [3:0] ALUSel_t, multiplexer_2_out, multiplexer_3_out, multiplexer_4_out, multiplexer_5_out,
       multiplexer_7_out, multiplexer_8_out, multiplexer_12_out, multiplexer_16_out, multiplexer_21_out;

  Comparator #(.width(7)) comparator_1 (.a(INSTRUCTION[6:0]), .b(7'b0010011), .eq(comparator_1_eq));  // open: gt, lt
  Comparator #(.width(7)) comparator_2 (.a(INSTRUCTION[6:0]), .b(7'b0000011), .eq(comparator_2_eq));  // open: gt, lt
  Comparator #(.width(7)) comparator_3 (.a(INSTRUCTION[6:0]), .b(7'b1100111), .eq(comparator_3_eq));  // open: gt, lt
  Comparator #(.width(7)) comparator_4 (.a(INSTRUCTION[6:0]), .b(7'b0010011), .eq(comparator_4_eq));  // open: gt, lt
  Comparator #(.width(7)) comparator_5 (.a(INSTRUCTION[6:0]), .b(7'b0100011), .eq(comparator_5_eq));  // open: gt, lt
  Comparator #(.width(7)) comparator_6 (.a(INSTRUCTION[6:0]), .b(7'b1100011), .eq(comparator_6_eq));  // open: gt, lt
  Comparator #(.width(7)) comparator_7 (.a(INSTRUCTION[6:0]), .b(7'b0110111), .eq(lui));  // open: gt, lt
  Comparator #(.width(7)) comparator_8 (.a(INSTRUCTION[6:0]), .b(7'b1101111), .eq(jal));  // open: gt, lt
  Comparator #(.width(7)) comparator_9 (.a(INSTRUCTION[6:0]), .b(7'b0110011), .eq(comparator_9_eq));  // open: gt, lt
  Comparator #(.width(3)) comparator_10 (.a(INSTRUCTION[14:12]), .b(3'b001), .eq(comparator_10_eq));  // open: gt, lt
  Comparator #(.width(3)) comparator_11 (.a(INSTRUCTION[14:12]), .b(3'b000), .eq(comparator_11_eq));  // open: gt, lt
  Comparator #(.width(3)) comparator_12 (.a(INSTRUCTION[14:12]), .b(3'b000), .eq(comparator_12_eq));  // open: gt, lt
  Comparator #(.width(3)) comparator_13 (.a(INSTRUCTION[14:12]), .b(3'b010), .eq(comparator_13_eq));  // open: gt, lt
  Comparator #(.width(3)) comparator_14 (.a(INSTRUCTION[14:12]), .b(3'b000), .eq(comparator_14_eq));  // open: gt, lt
  Comparator #(.width(3)) comparator_15 (.a(INSTRUCTION[14:12]), .b(3'b010), .eq(comparator_15_eq));  // open: gt, lt
  Comparator #(.width(3)) comparator_16 (.a(INSTRUCTION[14:12]), .b(3'b100), .eq(comparator_16_eq));  // open: gt, lt
  Comparator #(.width(3)) comparator_17 (.a(INSTRUCTION[14:12]), .b(3'b110), .eq(comparator_17_eq));  // open: gt, lt
  Comparator #(.width(3)) comparator_18 (.a(INSTRUCTION[14:12]), .b(3'b111), .eq(comparator_18_eq));  // open: gt, lt
  Comparator #(.width(3)) comparator_19 (.a(INSTRUCTION[14:12]), .b(3'b010), .eq(comparator_19_eq));  // open: gt, lt
  Comparator #(.width(3)) comparator_20 (.a(INSTRUCTION[14:12]), .b(3'b000), .eq(comparator_20_eq));  // open: gt, lt
  Comparator #(.width(3)) comparator_21 (.a(INSTRUCTION[14:12]), .b(3'b100), .eq(comparator_21_eq));  // open: gt, lt
  Comparator #(.width(3)) comparator_22 (.a(INSTRUCTION[14:12]), .b(3'b110), .eq(comparator_22_eq));  // open: gt, lt
  Comparator #(.width(3)) comparator_23 (.a(INSTRUCTION[14:12]), .b(3'b001), .eq(comparator_23_eq));  // open: gt, lt
  Comparator #(.width(3)) comparator_24 (.a(INSTRUCTION[14:12]), .b(3'b000), .eq(comparator_24_eq));  // open: gt, lt
  Comparator #(.width(3)) comparator_25 (.a(INSTRUCTION[14:12]), .b(3'b000), .eq(comparator_25_eq));  // open: gt, lt
  Comparator #(.width(3)) comparator_26 (.a(INSTRUCTION[14:12]), .b(3'b000), .eq(comparator_26_eq));  // open: gt, lt
  Comparator #(.width(3)) comparator_27 (.a(INSTRUCTION[14:12]), .b(3'b001), .eq(comparator_27_eq));  // open: gt, lt
  Comparator #(.width(3)) comparator_28 (.a(INSTRUCTION[14:12]), .b(3'b001), .eq(comparator_28_eq));  // open: gt, lt
  Comparator #(.width(3)) comparator_29 (.a(INSTRUCTION[14:12]), .b(3'b011), .eq(comparator_29_eq));  // open: gt, lt
  Comparator #(.width(3)) comparator_30 (.a(INSTRUCTION[14:12]), .b(3'b010), .eq(comparator_30_eq));  // open: gt, lt
  Comparator #(.width(3)) comparator_31 (.a(INSTRUCTION[14:12]), .b(3'b100), .eq(comparator_31_eq));  // open: gt, lt
  Comparator #(.width(3)) comparator_32 (.a(INSTRUCTION[14:12]), .b(3'b101), .eq(comparator_32_eq));  // open: gt, lt
  Comparator #(.width(3)) comparator_33 (.a(INSTRUCTION[14:12]), .b(3'b101), .eq(comparator_33_eq));  // open: gt, lt
  Comparator #(.width(3)) comparator_34 (.a(INSTRUCTION[14:12]), .b(3'b110), .eq(comparator_34_eq));  // open: gt, lt
  Comparator #(.width(3)) comparator_35 (.a(INSTRUCTION[14:12]), .b(3'b111), .eq(comparator_35_eq));  // open: gt, lt
  Comparator #(.width(3)) comparator_36 (.a(INSTRUCTION[14:12]), .b(3'b111), .eq(comparator_36_eq));  // open: gt, lt
  Comparator #(.width(3)) comparator_37 (.a(INSTRUCTION[14:12]), .b(3'b001), .eq(comparator_37_eq));  // open: gt, lt
  Comparator #(.width(3)) comparator_38 (.a(INSTRUCTION[14:12]), .b(3'b101), .eq(comparator_38_eq));  // open: gt, lt
  Comparator #(.width(3)) comparator_39 (.a(INSTRUCTION[14:12]), .b(3'b101), .eq(comparator_39_eq));  // open: gt, lt
  Comparator #(.width(7)) comparator_40 (.a(INSTRUCTION[31:25]), .b({7{1'b0}}), .eq(comparator_40_eq));  // open: gt, lt
  and and_1 (jalr, comparator_11_eq, comparator_2_eq);
  and and_2 (lb, comparator_12_eq, comparator_3_eq);
  and and_3 (lh, comparator_10_eq, comparator_3_eq);
  and and_4 (lw, comparator_13_eq, comparator_3_eq);
  and and_5 (addi, comparator_14_eq, comparator_4_eq);
  and and_6 (slti, comparator_15_eq, comparator_4_eq);
  and and_7 (xori, comparator_16_eq, comparator_4_eq);
  and and_8 (ori, comparator_17_eq, comparator_4_eq);
  and and_9 (andi, comparator_18_eq, comparator_4_eq);
  and and_10 (sw, comparator_19_eq, comparator_5_eq);
  and and_11 (beq, comparator_20_eq, comparator_6_eq);
  and and_12 (blt, comparator_21_eq, comparator_6_eq);
  and and_13 (bltu, comparator_22_eq, comparator_6_eq);
  and and_14 (bne, comparator_23_eq, comparator_6_eq);
  Comparator #(.width(7)) comparator_41 (
    .a(INSTRUCTION[31:25]), .b(7'b0000001), .eq(comparator_41_eq));  // open: gt, lt
  Comparator #(.width(7)) comparator_42 (
    .a(INSTRUCTION[31:25]), .b(7'b0100000), .eq(comparator_42_eq));  // open: gt, lt
  Comparator #(.width(7)) comparator_43 (.a(INSTRUCTION[31:25]), .b({7{1'b0}}), .eq(comparator_43_eq));  // open: gt, lt
  Comparator #(.width(7)) comparator_44 (
    .a(INSTRUCTION[31:25]), .b(7'b0000001), .eq(comparator_44_eq));  // open: gt, lt
  Comparator #(.width(7)) comparator_45 (
    .a(INSTRUCTION[31:25]), .b(7'b0000001), .eq(comparator_45_eq));  // open: gt, lt
  Comparator #(.width(7)) comparator_46 (.a(INSTRUCTION[31:25]), .b({7{1'b0}}), .eq(comparator_46_eq));  // open: gt, lt
  Comparator #(.width(7)) comparator_47 (.a(INSTRUCTION[31:25]), .b({7{1'b0}}), .eq(comparator_47_eq));  // open: gt, lt
  Comparator #(.width(7)) comparator_48 (
    .a(INSTRUCTION[31:25]), .b(7'b0000001), .eq(comparator_48_eq));  // open: gt, lt
  Comparator #(.width(7)) comparator_49 (.a(INSTRUCTION[31:25]), .b({7{1'b0}}), .eq(comparator_49_eq));  // open: gt, lt
  Comparator #(.width(7)) comparator_50 (.a(INSTRUCTION[31:25]), .b({7{1'b0}}), .eq(comparator_50_eq));  // open: gt, lt
  Comparator #(.width(7)) comparator_51 (
    .a(INSTRUCTION[31:25]), .b(7'b0000001), .eq(comparator_51_eq));  // open: gt, lt
  Comparator #(.width(7)) comparator_52 (.a(INSTRUCTION[31:25]), .b({7{1'b0}}), .eq(comparator_52_eq));  // open: gt, lt
  Comparator #(.width(7)) comparator_53 (.a(INSTRUCTION[31:25]), .b({7{1'b0}}), .eq(comparator_53_eq));  // open: gt, lt
  Comparator #(.width(7)) comparator_54 (.a(INSTRUCTION[31:25]), .b({7{1'b0}}), .eq(comparator_54_eq));  // open: gt, lt
  Comparator #(.width(7)) comparator_55 (
    .a(INSTRUCTION[31:25]), .b(7'b0100000), .eq(comparator_55_eq));  // open: gt, lt
  and and_15 (add, comparator_40_eq, comparator_24_eq, comparator_9_eq);
  and and_16 (mul, comparator_41_eq, comparator_25_eq, comparator_9_eq);
  and and_17 (sub, comparator_42_eq, comparator_26_eq, comparator_9_eq);
  and and_18 (sll0, comparator_43_eq, comparator_27_eq, comparator_9_eq);
  and and_19 (mulh, comparator_44_eq, comparator_28_eq, comparator_9_eq);
  and and_20 (mulhu, comparator_45_eq, comparator_29_eq, comparator_9_eq);
  and and_21 (slt, comparator_46_eq, comparator_30_eq, comparator_9_eq);
  and and_22 (xor0, comparator_47_eq, comparator_31_eq, comparator_9_eq);
  and and_23 (divu, comparator_48_eq, comparator_32_eq, comparator_9_eq);
  and and_24 (srl0, comparator_49_eq, comparator_33_eq, comparator_9_eq);
  and and_25 (or0, comparator_50_eq, comparator_34_eq, comparator_9_eq);
  and and_26 (remu, comparator_51_eq, comparator_35_eq, comparator_9_eq);
  and and_27 (and0, comparator_52_eq, comparator_36_eq, comparator_9_eq);
  and and_28 (slli, comparator_53_eq, comparator_37_eq, comparator_1_eq);
  and and_29 (srli, comparator_54_eq, comparator_38_eq, comparator_1_eq);
  and and_30 (srai, comparator_55_eq, comparator_39_eq, comparator_1_eq);
  Comparator #(.width(7)) comparator_56 (
    .a(7'b0110011), .b(INSTRUCTION[6:0]), .gt(comparator_56_gt), .eq(R_TYPE), .lt(comparator_56_lt));
  Comparator #(.width(7)) comparator_57 (
    .a(7'b0110011), .b(INSTRUCTION[6:0]), .gt(comparator_56_gt), .eq(R_TYPE), .lt(comparator_56_lt));
  Comparator #(.width(7)) comparator_58 (.a(7'b0000011), .b(INSTRUCTION[6:0]), .eq(I_TYPE_LOAD));  // open: gt, lt
  Comparator #(.width(7)) comparator_59 (.a(7'b0010011), .b(INSTRUCTION[6:0]), .eq(I_TYPE));  // open: gt, lt
  Comparator #(.width(7)) comparator_60 (.a(7'b0110111), .b(INSTRUCTION[6:0]), .eq(U_TYPE));  // open: gt, lt
  Comparator #(.width(7)) comparator_61 (.a(7'b1100011), .b(INSTRUCTION[6:0]), .eq(SB_TYPE));  // open: gt, lt
  Comparator #(.width(7)) comparator_62 (.a(7'b1100111), .b(INSTRUCTION[6:0]), .eq(JALR_I_TYPE));  // open: gt, lt
  Comparator #(.width(7)) comparator_63 (.a(7'b1101111), .b(INSTRUCTION[6:0]), .eq(UJ_TYPE));  // open: gt, lt
  Comparator #(.width(7)) comparator_64 (.a(7'b0100011), .b(INSTRUCTION[6:0]), .eq(MEMRW));  // open: gt, lt
  not not_1 (BSEL, R_TYPE);
  or or_1 (ASEL, SB_TYPE, UJ_TYPE);
  nor nor_1 (REGWEN, MEMRW, SB_TYPE);
  not not_2 (not_2_out, BrEq);
  Multiplexer #(.select(3), .enable("false")) multiplexer_1 (
    .in0(BrEq), .in1(not_2_out), .in4(BrLT), .out(multiplexer_1_out), .sel(INSTRUCTION[14:12]));  // open: in2, in3, in5, in6, in7
  Multiplexer #(.width(4), .enable("false")) multiplexer_2 (
    .in0(4'b0000), .in1(4'b1010), .out(multiplexer_2_out), .sel(INSTRUCTION[25]));
  Multiplexer #(.width(4), .enable("false")) multiplexer_3 (
    .in0(4'b0110), .in1(4'b1110), .out(multiplexer_3_out), .sel(INSTRUCTION[25]));
  Multiplexer #(.width(4), .enable("false")) multiplexer_4 (
    .in0(4'b0100), .in1(4'b1000), .out(multiplexer_4_out), .sel(INSTRUCTION[25]));
  Multiplexer #(.width(4), .enable("false")) multiplexer_5 (
    .in0(4'b0100), .in1(4'b0101), .out(multiplexer_5_out), .sel(INSTRUCTION[30]));
  or or_2 (or_2_out, jalr, UJ_TYPE);
  and and_31 (and_31_out, SB_TYPE, multiplexer_1_out);
  Multiplexer #(.width(3), .enable("false")) multiplexer_6 (
    .in1(3'b000), .out(multiplexer_6_out), .sel(R_TYPE));  // open: in0
  or or_3 (PCSEL, or_2_out, and_31_out);
  Multiplexer #(.width(4), .enable("false")) multiplexer_7 (
    .in0(multiplexer_2_out), .in1(4'b1000), .out(multiplexer_7_out), .sel(INSTRUCTION[30]));
  Multiplexer #(.select(3), .width(4), .enable("false")) multiplexer_8 (
    .in0(4'b0000), .in1(4'b0110), .in2(4'b0111), .in4(4'b0011), .in5(multiplexer_5_out), .in6(4'b0010),
    .in7(4'b0001), .out(multiplexer_8_out), .sel(INSTRUCTION[14:12]));  // open: in3
  Multiplexer #(.enable("false")) multiplexer_9 (.in0(1'b0), .in1(1'b1), .out(multiplexer_9_out), .sel(SB_TYPE));
  Multiplexer #(.width(3), .enable("false")) multiplexer_10 (
    .in0(multiplexer_6_out), .in1(3'b001), .out(multiplexer_10_out), .sel(or_4_out));
  or or_4 (or_4_out, I_TYPE_LOAD, jalr, I_TYPE);
  Multiplexer #(.width(2), .enable("false")) multiplexer_11 (
    .in1(2'b00), .out(multiplexer_11_out), .sel(I_TYPE_LOAD));  // open: in0
  Multiplexer #(.width(4), .enable("false")) multiplexer_12 (
    .in0(4'b0001), .in1(4'b1001), .out(multiplexer_12_out), .sel(INSTRUCTION[25]));
  Multiplexer #(.select(3), .enable("false")) multiplexer_13 (
    .in4(1'b0), .in6(multiplexer_9_out), .sel(INSTRUCTION[14:12]));  // open: in0, in1, in2, in3, in5, in7, out
  Multiplexer #(.width(3), .enable("false")) multiplexer_14 (
    .in0(multiplexer_10_out), .in1(3'b010), .out(multiplexer_14_out), .sel(MEMRW));
  Multiplexer #(.width(2), .enable("false")) multiplexer_15 (
    .in0(multiplexer_11_out), .in1(2'b01), .out(multiplexer_15_out), .sel(or_5_out));
  or or_5 (or_5_out, U_TYPE, I_TYPE, R_TYPE);
  Multiplexer #(.select(3), .width(4), .enable("false")) multiplexer_16 (
    .in0(multiplexer_7_out), .in1(multiplexer_3_out), .in2(4'b0111), .in3(4'b1011), .in4(4'b0011),
    .in5(multiplexer_4_out), .in6(4'b0010), .in7(multiplexer_12_out), .out(multiplexer_16_out),
    .sel(INSTRUCTION[14:12]));
  Multiplexer #(.width(3), .enable("false")) multiplexer_17 (
    .in0(multiplexer_14_out), .in1(3'b011), .out(multiplexer_17_out), .sel(SB_TYPE));
  Multiplexer #(.width(2), .enable("false")) multiplexer_18 (
    .in0(multiplexer_15_out), .in1(2'b10), .out(WBSEL), .sel(or_6_out));
  or or_6 (or_6_out, UJ_TYPE, jalr);
  Multiplexer #(.width(3), .enable("false")) multiplexer_19 (
    .in0(multiplexer_17_out), .in1(3'b100), .out(multiplexer_19_out), .sel(U_TYPE));
  Multiplexer #(.width(3), .enable("false")) multiplexer_20 (
    .in0(multiplexer_19_out), .in1(3'b101), .out(IMMSEL), .sel(UJ_TYPE));
  Multiplexer #(.width(4), .enable("false")) multiplexer_21 (
    .in0(4'b0000), .in1(multiplexer_16_out), .out(multiplexer_21_out), .sel(R_TYPE));
  Multiplexer #(.width(4), .enable("false")) multiplexer_22 (
    .in0(multiplexer_21_out), .in1(multiplexer_8_out), .out(ALUSel_t), .sel(I_TYPE));

  // Other names for the same wires on the sheet: OPCODE[6:0] = INSTRUCTION[6:0]; rd[4:0] = INSTRUCTION[11:7];
  //   FUNCT3[2:0] = INSTRUCTION[14:12]; rs1[4:0] = INSTRUCTION[19:15]; I_IMM[11:0] = INSTRUCTION[31:20];
  //   rs2[4:0] = INSTRUCTION[24:20]; SHAMT[4:0] = INSTRUCTION[24:20]; F7_Bit0 = INSTRUCTION[25];
  //   FUNCT7[6:0] = INSTRUCTION[31:25]; F7_Bit5 = INSTRUCTION[30]; S_TYPE = MEMRW

  // Notes on the sheet:
  //   INPUTS
  //   I-Type
  //   shifts
  //   (imms)
  //   (jalr)
  //   R-Type
  //   Note that in slli/srli/srai "funct7" is actually the upper 7 bits of the immediate. 
  //   Get Instruction Type
  //   BSEL LOGIC
  //   BSel = 1 represents selection of an Immediate. This will be 1 for all cases EXCEPT R-type instructions
  //   ASEL LOGIC
  //   ASEL= 1 ONLY on jumps and branches
  //   REGWEN LOGIC
  //   RegWEN = 0 if we want to read DataA output, or 1 if we want PC value.
  //   PCSEL LOGIC
  //   PCSEL = 1 IFF jump instruction OR if branch instruction and the branch comparison evaluates true.
  //   NOTE: BrEq and BrLT are NOT evaluated until the results from branch operator return.
  //   ALUSEL LOGIC
  //   Only funct3 and funct7 are needed to determine the kind of ALU operation.
  //   Bits 0 and 5 of FUNCT 7 (in an R-Type function) represent the two digits of the HEXIDECIMAL equivalent of FUNCT7. 
  //   BrUn LOGIC
  //   Funct3 serves as the data selector from a mux. We only need to look at funct3's for SB-type instructions
  //   If Funct3 = 0x4, we know that it's BLT- doing SIGNED COMPARISON, so BrUn = 0
  //   If funct3 = 0x6 AND SB_TYPE is 1, then we must be doing BLTU, so BrUn = 1 (unsigned comparison)
  //   IMMSEL LOGIC
  //   Select bit of Immediate Generator Based on Type of Instruction
  //   MEMRW LOGIC
  //   MemRW is only 1 on store instructions
  //   WBSEL LOGIC
  //   WBSEL= 0 on load instructions
  //   WBSEL= 1 on instructions that require ALU OUTPUT to rd: R-type, I-type, OR lui
  //   WBSEL= 2 on instructions that require rd = PC+4
  //   OUTPUTS OF CONTROL
endmodule

module ImmGen (
  input  [31:0] INSTRUCTION,
  input  [31:0] in_2,
  input  [2:0] IMMSEL,
  output [31:0] IMMEDIATE_GENERATED
);

  wire [31:0] I_IMM, S_IMM, SB_IMM;
  wire [31:20] UJ_IMM;

  assign UJ_IMM = {{11{INSTRUCTION[31]}}, INSTRUCTION[31]};  // Bit_Extender bit_extender_1
  // Probe on I_IMM
  assign I_IMM = {{20{INSTRUCTION[31]}}, INSTRUCTION[31:20]};  // Bit_Extender bit_extender_2
  // Probe on S_IMM
  assign SB_IMM = {{19{INSTRUCTION[31]}}, {INSTRUCTION[31], INSTRUCTION[7], INSTRUCTION[30:25], INSTRUCTION[11:8], 1'b0}};  // Bit_Extender bit_extender_3
  assign S_IMM = {{20{INSTRUCTION[31]}}, {INSTRUCTION[31:25], INSTRUCTION[11:7]}};  // Bit_Extender bit_extender_4
  Multiplexer #(.select(3), .width(32), .enable("false")) multiplexer_1 (
    .in0({32{1'b0}}), .in1(I_IMM), .in2(S_IMM), .in3(SB_IMM), .in4({INSTRUCTION[31:12], {12{1'b0}}}),
    .in5({UJ_IMM, INSTRUCTION[19:12], INSTRUCTION[20], INSTRUCTION[30:21], 1'b0}), .out(IMMEDIATE_GENERATED),
    .sel(IMMSEL));  // open: in6, in7

  // Other names for the same wires on the sheet: U_IMM[31:12] = INSTRUCTION[31:12];
  //   UJ_IMM[19:1] = {INSTRUCTION[19:12], INSTRUCTION[20], INSTRUCTION[30:21]}
endmodule

module BranchComp (
  input  [31:0] DataA,
  input  [31:0] DataB,
  input  BrUn,
  output BrLT,
  output BrEq
);

  wire and_1_out, and_2_out, and_3_out, and_4_out, comparator_1_eq, comparator_2_eq, comparator_3_lt,
       comparator_4_eq, comparator_5_eq, comparator_6_lt;

  Comparator #(.width(1)) comparator_1 (.a(BrUn), .b(1'b0), .eq(comparator_1_eq));  // open: gt, lt
  Comparator #(.width(1)) comparator_2 (.a(BrUn), .b(1'b1), .eq(comparator_2_eq));  // open: gt, lt
  Comparator #(.width(32), .mode("unsigned")) comparator_3 (
    .a(DataA), .b(DataB), .lt(comparator_3_lt));  // open: gt, eq
  Comparator #(.width(32)) comparator_4 (.a(DataA), .b(DataB), .eq(comparator_4_eq));  // open: gt, lt
  Comparator #(.width(32), .mode("unsigned")) comparator_5 (
    .a(DataA), .b(DataB), .eq(comparator_5_eq));  // open: gt, lt
  Comparator #(.width(32)) comparator_6 (.a(DataA), .b(DataB), .lt(comparator_6_lt));  // open: gt, eq
  and and_1 (and_1_out, comparator_3_lt, comparator_2_eq);
  and and_2 (and_2_out, comparator_6_lt, comparator_1_eq);
  and and_3 (and_3_out, comparator_1_eq, comparator_4_eq);
  and and_4 (and_4_out, comparator_2_eq, comparator_5_eq);
  or or_1 (BrLT, and_1_out, and_2_out);
  or or_2 (BrEq, and_3_out, and_4_out);

  // Notes on the sheet:
  //   Signed
  //   Unsigned
  //   INPUTS
endmodule

module TempSubcircs (
);

  wire add, and0, and_3_p3, beq, blt, bltu, bne, BrEq, BrLT, bsel, clk, divu, jal, jalr, mul, mulh, mulhu,
       or0, PCSEL, remu, sll0, slt, sra0, srl0, sub, undriven, undriven_2, undriven_3, undriven_4, xor0;
  wire [3:0] ALUSEL;
  wire [31:0] ALU_OUT, multiplexer_1_out, PC_PLUS_4_TELEPORT, PROGRAM_COUNTER;

  // Probe on PROGRAM_COUNTER
  Adder #(.width(32)) adder_1 (.a(PROGRAM_COUNTER), .b(32'h4), .out(PC_PLUS_4_TELEPORT));  // open: cin, cout
  Multiplexer #(.width(32), .enable("false")) multiplexer_1 (
    .in0(PC_PLUS_4_TELEPORT), .in1(ALU_OUT), .out(multiplexer_1_out), .sel(PCSEL));
  Register #(.width(32)) register_1 (.D(multiplexer_1_out), .clk(clk), .Q(PROGRAM_COUNTER));  // open: en, clr
  Priority_Encoder #(.select(4)) priority_encoder_1 (
    .in0(add), .in1(and0), .in2(or0), .in3(xor0), .in4(srl0), .in5(sra0), .in6(sll0), .in7(slt), .in8(divu),
    .in9(remu), .in10(mul), .in11(mulhu), .in12(sub), .in13(bsel), .in14(mulh), .out(ALUSEL));  // open: in15, gs, en_out, en_in
  // NOT_Gate not_1 has open pins: in=beq, out=open
  // AND_Gate and_1 has open pins: in0=bltu, in1=BrLT, out=open
  // AND_Gate and_2 has open pins: in0=bne, in1=undriven, out=open
  // AND_Gate and_3: pin names not known; wires that end beside it: BrEq, beq, and_3_p3
  // AND_Gate and_4 has open pins: in0=blt, in1=BrLT, out=open
  // OR_Gate or_1 has open pins: in0=and_3_p3, in1=undriven_3, in2=undriven_2, in3=undriven_4, in4=jalr, in5=jal, out=open
endmodule
