// Logisim project regfile.circ as structural Verilog: 1 circuit, main circuit main
module main (
  input  [4:0] rs1,
  input  [4:0] rs2,
  input  [4:0] rd,
  input  [31:0] Write_Data,
  input  RegWEn,
  input  clk,
  output [31:0] ra,
  output [31:0] sp,
  output [31:0] t0,
  output [31:0] t1,
  output [31:0] t2,
  output [31:0] s0,
  output [31:0] s1,
  output [31:0] a0,
  output [31:0] Read_Data_1,
  output [31:0] Read_Data_2
);

  wire and_1_out, and_2_out, and_3_out, and_4_out, and_5_out, and_6_out, and_7_out, and_8_out, write_a0,
       write_ra, write_s0, write_s1, write_sp, write_t0, write_t1, write_t2;
  wire [31:0] multiplexer_2_out, multiplexer_3_out, multiplexer_4_out, multiplexer_5_out, multiplexer_7_out,
       multiplexer_8_out, multiplexer_9_out, multiplexer_10_out;

  Multiplexer #(.select(5), .width(32), .enable("false")) multiplexer_1 (
    .in0({32{1'b0}}), .in1(ra), .in2(sp), .in5(t0), .in6(t1), .in7(t2), .in8(s0), .in9(s1), .in10(a0),
    .out(Read_Data_1), .sel(rs1));  // open: in3, in4, in11, in12, in13, in14, in15, in16, in17, in18, in19, in20, in21, in22, in23, in24, in25, in26, in27, in28, in29, in30, in31
  Multiplexer #(.width(32)) multiplexer_2 (
    .in0(ra), .in1(Write_Data), .out(multiplexer_2_out), .sel(and_1_out));  // open: en
  and and_1 (and_1_out, RegWEn, write_ra);
  Multiplexer #(.width(32)) multiplexer_3 (
    .in0(t0), .in1(Write_Data), .out(multiplexer_3_out), .sel(and_2_out));  // open: en
  and and_2 (and_2_out, RegWEn, write_t0);
  Multiplexer #(.width(32)) multiplexer_4 (
    .in0(t2), .in1(Write_Data), .out(multiplexer_4_out), .sel(and_3_out));  // open: en
  and and_3 (and_3_out, RegWEn, write_t2);
  Multiplexer #(.width(32)) multiplexer_5 (
    .in0(s1), .in1(Write_Data), .out(multiplexer_5_out), .sel(and_4_out));  // open: en
  and and_4 (and_4_out, RegWEn, write_s1);
  Register #(.width(32)) regRA (.D(multiplexer_2_out), .clk(clk), .Q(ra));  // open: en, clr
  Register #(.width(32)) regT0 (.D(multiplexer_3_out), .clk(clk), .Q(t0));  // open: en, clr
  Register #(.width(32)) regT2 (.D(multiplexer_4_out), .clk(clk), .Q(t2));  // open: en, clr
  Register #(.width(32)) regS1 (.D(multiplexer_5_out), .clk(clk), .Q(s1));  // open: en, clr
  Multiplexer #(.select(5), .width(32), .enable("false")) multiplexer_6 (
    .in0({32{1'b0}}), .in1(ra), .in2(sp), .in5(t0), .in6(t1), .in7(t2), .in8(s0), .in9(s1), .in10(a0),
    .out(Read_Data_2), .sel(rs2));  // open: in3, in4, in11, in12, in13, in14, in15, in16, in17, in18, in19, in20, in21, in22, in23, in24, in25, in26, in27, in28, in29, in30, in31
  Multiplexer #(.width(32)) multiplexer_7 (
    .in0(sp), .in1(Write_Data), .out(multiplexer_7_out), .sel(and_5_out));  // open: en
  and and_5 (and_5_out, RegWEn, write_sp);
  Multiplexer #(.width(32)) multiplexer_8 (
    .in0(t1), .in1(Write_Data), .out(multiplexer_8_out), .sel(and_6_out));  // open: en
  and and_6 (and_6_out, RegWEn, write_t1);
  Multiplexer #(.width(32)) multiplexer_9 (
    .in0(s0), .in1(Write_Data), .out(multiplexer_9_out), .sel(and_7_out));  // open: en
  and and_7 (and_7_out, RegWEn, write_s0);
  Multiplexer #(.width(32)) multiplexer_10 (
    .in0(a0), .in1(Write_Data), .out(multiplexer_10_out), .sel(and_8_out));  // open: en
  and and_8 (and_8_out, RegWEn, write_a0);
  Register #(.width(32)) RegSP (.D(multiplexer_7_out), .clk(clk), .Q(sp));  // open: en, clr
  Register #(.width(32)) regT1 (.D(multiplexer_8_out), .clk(clk), .Q(t1));  // open: en, clr
  Register #(.width(32)) regS0 (.D(multiplexer_9_out), .clk(clk), .Q(s0));  // open: en, clr
  Register #(.width(32)) regA0 (.D(multiplexer_10_out), .clk(clk), .Q(a0));  // open: en, clr
  Demultiplexer #(.select(5), .enable("false")) demultiplexer_1 (
    .out1(write_ra), .out2(write_sp), .out5(write_t0), .out6(write_t1), .out7(write_t2), .out8(write_s0),
    .out9(write_s1), .out10(write_a0), .in(1'b1), .sel(rd));  // open: out0, out3, out4, out11, out12, out13, out14, out15, out16, out17, out18, out19, out20, out21, out22, out23, out24, out25, out26, out27, out28, out29, out30, out31

  // Other names for the same wires on the sheet: a0_out[31:0] = a0; ra_out[31:0] = ra; read_data1[31:0] = Read_Data_1;
  //   read_data2[31:0] = Read_Data_2; read_reg1[4:0] = rs1; read_reg2[4:0] = rs2; s0_out[31:0] = s0;
  //   s1_out[31:0] = s1; sp_out[31:0] = sp; t0_out[31:0] = t0; t1_out[31:0] = t1; t2_out[31:0] = t2;
  //   write_en = RegWEn; write_reg[4:0] = rd

  // Notes on the sheet:
  //   INPUTS to your circuit
  //   Select which (2) registers to read from. Inputs are VALUES of each register
  //   DON'T CHANGE THE LOCATIONS OF THE INPUTS AND OUTPUTS!
  //   These are DEBUG/TEST outputs from your circuit.
  //   Select which register to allow writing to. Outputs are single-bit indicators.
  //   OUTPUTS from your circuit
endmodule
