// Logisim project cpu.circ as structural Verilog: 1 circuit, main circuit main
module main (
  input  [31:0] INSTRUCTION,
  input  CLOCK,
  output [31:0] PROGRAM_COUNTER,
  output [31:0] ra,
  output [31:0] sp,
  output [31:0] t0,
  output [31:0] t1,
  output [31:0] t2,
  output [31:0] s0,
  output [31:0] s1,
  output [31:0] a0
);

  wire DMEM_p1, DMEM_p5;
  wire [31:0] adder_1_out, Arithmetic_Logic_Unit_result, DMEM_p2, imm, INSTRUCTION_t, multiplexer_1_out,
       RegFile_read_data_1, RegFile_read_data_2;

  Adder #(.width(32)) adder_1 (.a(PROGRAM_COUNTER), .b(32'h4), .out(adder_1_out));  // open: cin, cout
  Register #(.width(32)) PC (.D(adder_1_out), .clk(CLOCK), .Q(PROGRAM_COUNTER));  // open: en, clr
  // Probe on INSTRUCTION_t
  // Probe on INSTRUCTION_t[31:20]
  // Probe on INSTRUCTION_t[11:7]
  // Probe on INSTRUCTION_t[19:15]
  assign imm = {{20{INSTRUCTION_t[31]}}, INSTRUCTION_t[31:20]};  // Bit_Extender bit_extender_1
  // Probe on imm
  Register #(.width(32)) register_1 (.D(INSTRUCTION), .clk(CLOCK), .Q(INSTRUCTION_t));  // open: en, clr
  regfile_main RegFile (
    .rs2(INSTRUCTION_t[24:20]), .rd(INSTRUCTION_t[11:7]), .Read_Data_1(RegFile_read_data_1),
    .Read_Data_2(RegFile_read_data_2), .ra(ra), .sp(sp), .t0(t0), .t1(t1), .t2(t2), .s0(s0), .s1(s1),
    .a0(a0), .rs1(INSTRUCTION_t[19:15]), .Write_Data(multiplexer_1_out), .RegWEn(1'b1), .clk(CLOCK));
  alu Arithmetic_Logic_Unit (.ALUSel(4'b0000), .B(imm), .A(RegFile_read_data_1), .Result(Arithmetic_Logic_Unit_result));
  // Probe on Arithmetic_Logic_Unit_result
  Multiplexer #(.select(2), .width(32), .enable("false")) multiplexer_1 (
    .in0(Arithmetic_Logic_Unit_result), .in1(DMEM_p2), .out(multiplexer_1_out), .sel(2'b00));  // open: in2, in3
  // mem_main DMEM: pin names not known; wires that end beside it: DMEM_p1, DMEM_p2, DMEM_p1, CLOCK, DMEM_p5, 1'b0

  // Other names for the same wires on the sheet: clk = CLOCK; INSTRUCTION_F[31:0] = INSTRUCTION

  // Notes on the sheet:
  //   Output
  //   IMEM (do **NOT** move this)
  //   Inputs
  //   MUX here
  //   Inputs/Outputs for testing. Do **NOT** move these.
endmodule
